# Fritzing sketch at-me (saved by Fritzing 0.9.5d)
circuit board: 8.46667cm x 5.64444cm
breadboards: 2

parts:
  Componente1 = Arduino Nano (Rev3.0)
  DFRobot_DFPlayer_Mini1 = DFRobot DFPlayer Mini [part_number=DFR0299]
  S1 = Pushbutton [package="[THT]"]
  U2 = 3.5mm Audio Jack [package=audio-jack]
  R1 = Resistor [tolerance=±5% resistance=1k package=THT]
  LED1 = smd LED [color="Yellow (595nm)" package="1206 [SMD]"]
  R2 = Resistor [tolerance=±5% resistance=220 package=THT]
  S2 = Toggle Switch [package=THT]
  R3 = Resistor [tolerance=±5% resistance=10k package=THT]
  LED2 = LED - 5mm [color="Red (633nm)" package="5 mm [THT]"]
  R4 = Resistor [tolerance=±5% resistance=220 package=THT]

nets:
  N1: Componente1.GND, DFRobot_DFPlayer_Mini1.GND-1, DFRobot_DFPlayer_Mini1.GND-2, S1.Pin_1, S1.Pin_2, LED1.anode, R3.Pin_1, LED2.cathode
  N2: Componente1.D2, R2.Pin_0
  N3: Componente1.D3, S2.L1, R3.Pin_0
  N4: Componente1.D5, R4.Pin_0
  N5: Componente1.D6, S1.Pin_3, S1.Pin_4
  N6: Componente1.D10, DFRobot_DFPlayer_Mini1.TX
  N7: Componente1.D11/MOSI, R1.Pin_1
  5V: Componente1.5V, DFRobot_DFPlayer_Mini1.VCC, S2.COM
  N8: DFRobot_DFPlayer_Mini1.RX, R1.Pin_0
  N9: DFRobot_DFPlayer_Mini1.SPK_1, U2.LEFT
  N10: DFRobot_DFPlayer_Mini1.SPK_2, U2.RIGHT, U2.SLEEVE
  N11: LED1.cathode, R2.Pin_1
  N12: LED2.anode, R4.Pin_1
